// Logisim project Storage.circ as structural Verilog: 5 circuits, main circuit SimpleLatch
module SimpleLatch (
  input  In
);

  wire or_1_out;

  or or_1 (or_1_out, In, or_1_out);
  LED Out (.in(or_1_out));

  // Notes on the sheet:
  //   Creative Commons BY NC 4.0 International License
endmodule

module SRLatch (
  input  R,
  input  R_2,
  input  S,
  input  S_2
);

  wire nor_1_out, nor_2_out, or_1_out, or_2_out;

  nor nor_1 (nor_1_out, R, nor_2_out);
  nor nor_2 (nor_2_out, nor_1_out, S_2);
  // Probe on nor_1_out
  // Probe on nor_2_out
  // Probe on or_1_out
  or or_1 (or_1_out, R_2, or_2_out);
  // Probe on or_2_out
  or or_2 (or_2_out, or_1_out, S);

  // Notes on the sheet:
  //   Creative Commons BY NC 4.0 International License
  //   S-R Flip-Flop with OR Gates
  //   Both gates get stuck outputting a 1
endmodule

module WriteEnable (
  input  Set,
  input  R,
  input  Reset,
  input  EN,
  input  [1:0] Selector,
  input  S
);

  wire and_1_out, and_2_out, decoder_1_out0, decoder_1_out1, decoder_1_out2, decoder_1_out3, nor_1_out,
       nor_2_out;

  and and_1 (and_1_out, R, EN);
  and and_2 (and_2_out, EN, S);
  nor nor_1 (nor_1_out, and_1_out, nor_2_out);
  nor nor_2 (nor_2_out, nor_1_out, and_2_out);
  // Probe on nor_1_out
  // Probe on nor_2_out
  Decoder #(.select(2), .enable("false")) decoder_1 (
    .out0(decoder_1_out0), .out1(decoder_1_out1), .out2(decoder_1_out2), .out3(decoder_1_out3), .sel(Selector));
  S_R_Flip_Flop #(.trigger("high")) SR0__00 (
    .S(Set), .clk(decoder_1_out0), .R(Reset));  // open: Q, Qn, preset, reset, en
  S_R_Flip_Flop #(.trigger("high")) SR1__01 (
    .S(Set), .clk(decoder_1_out1), .R(Reset));  // open: Q, Qn, preset, reset, en
  S_R_Flip_Flop #(.trigger("high")) SR2__10 (
    .S(Set), .clk(decoder_1_out2), .R(Reset));  // open: Q, Qn, preset, reset, en
  S_R_Flip_Flop #(.trigger("high")) SR3__11 (
    .S(Set), .clk(decoder_1_out3), .R(Reset));  // open: Q, Qn, preset, reset, en

  // Notes on the sheet:
  //   Creative Commons BY NC 4.0 International License
endmodule

module DLatch (
  input  D,
  input  Input,
  input  EN,
  input  Enable,
  input  [1:0] Selector,
  input  D_2,
  input  EN_2
);

  wire and_1_out, and_2_out, and_3_out, and_4_out, clock_1_out, decoder_1_out0, decoder_1_out1,
       decoder_1_out2, decoder_1_out3, nor_1_out, nor_2_out, nor_3_out, nor_4_out;

  Clock clock_1 (.out(clock_1_out));
  and and_1 (and_1_out, ~D, EN);  // AND_Gate
  and and_2 (and_2_out, EN, D);
  and and_3 (and_3_out, ~D_2, EN_2, clock_1_out);  // AND_Gate
  and and_4 (and_4_out, D_2, EN_2, clock_1_out);
  nor nor_1 (nor_1_out, and_1_out, nor_2_out);
  nor nor_2 (nor_2_out, nor_1_out, and_2_out);
  // Probe on nor_1_out
  // Probe on nor_2_out
  nor nor_3 (nor_3_out, and_3_out, nor_4_out);
  // Probe on nor_3_out
  // Probe on nor_4_out
  nor nor_4 (nor_4_out, nor_3_out, and_4_out);
  Decoder #(.select(2)) decoder_1 (
    .out0(decoder_1_out0), .out1(decoder_1_out1), .out2(decoder_1_out2), .out3(decoder_1_out3),
    .sel(Selector), .en(Enable));
  D_Flip_Flop #(.trigger("high")) D0__00 (.clk(decoder_1_out0), .D(Input));  // open: Q, Qn, preset, en, reset
  D_Flip_Flop #(.trigger("high")) D1__01 (.clk(decoder_1_out1), .D(Input));  // open: Q, Qn, preset, en, reset
  D_Flip_Flop #(.trigger("high")) D2__10 (.clk(decoder_1_out2), .D(Input));  // open: Q, Qn, preset, en, reset
  D_Flip_Flop #(.trigger("high")) D3__11 (.clk(decoder_1_out3), .D(Input));  // open: Q, Qn, preset, en, reset

  // Notes on the sheet:
  //   Selector: pull=up
  //   D Latch
  //   D Flip-Flop
  //   Creative Commons BY NC 4.0 International License
endmodule

module RisingEdge (
  input  in_1,
  input  in_2,
  output out_3
);

  wire and_2_out, clock_1_out, not_1_out, not_2_out, not_3_out, not_4_out;

  Clock clock_1 (.out(clock_1_out));
  and and_1 (out_3, in_1, not_1_out);
  not not_1 (not_1_out, in_1);
  not not_2 (not_2_out, not_4_out);
  not not_3 (not_3_out, not_2_out);
  not not_4 (not_4_out, clock_1_out);
  and and_2 (and_2_out, clock_1_out, not_3_out);
  D_Flip_Flop d_ff_1 (.clk(and_2_out), .D(in_2));  // open: Q, Qn, preset, en, reset

  // Notes on the sheet:
  //   To use this circuit, Start the simulator's clock
  //   Simulate > Ticks Enabled
  //   Simulate > Tick Frequency > 1 Hz
  //   Creative Commons BY NC 4.0 International License
endmodule
