// Logisim project Control.circ as structural Verilog: 2 circuits, main circuit Decoder
module Decoder (
  input  A,
  input  B,
  input  Bit8,
  input  Bit7,
  input  [1:0] A_B
);

  wire Add_out, and_1_out, and_2_out, and_3_out, and_4_out, decoder_1_out0, decoder_1_out1, decoder_1_out2,
       decoder_1_out3, Div_out, Mul_out, Sub_out;

  Decoder_part #(.select(2)) decoder_1 (
    .out0(decoder_1_out0), .out1(decoder_1_out1), .out2(decoder_1_out2), .out3(decoder_1_out3), .sel(A_B));  // open: en
  LED D0 (.in(and_1_out));
  and and_1 (and_1_out, ~A, ~B);  // AND_Gate
  LED D1 (.in(and_2_out));
  and and_2 (and_2_out, ~A, B);  // AND_Gate
  and and_3 (and_3_out, A, ~B);  // AND_Gate
  LED D2 (.in(and_3_out));
  and and_4 (and_4_out, A, B);
  LED D3 (.in(and_4_out));
  LED D0_2 (.in(decoder_1_out0));
  LED D1_2 (.in(decoder_1_out1));
  LED D2_2 (.in(decoder_1_out2));
  LED D3_2 (.in(decoder_1_out3));
  and Add (Add_out, ~Bit8, ~Bit7);  // AND_Gate
  and Sub (Sub_out, ~Bit8, Bit7);  // AND_Gate
  and Mul (Mul_out, Bit8, ~Bit7);  // AND_Gate
  and Div (Div_out, Bit8, Bit7);

  // Notes on the sheet:
  //   Input to
  //   Operation
  //   Selector
endmodule

module Multiplexer (
  input  A3,
  input  A2,
  input  A1,
  input  A0,
  input  S0,
  input  S1,
  input  A3_2,
  input  A2_2,
  input  A1_2,
  input  A0_2,
  input  [1:0] S1_S0
);

  wire and_1_out, and_2_out, and_3_out, and_4_out, multiplexer_1_out, or_1_out;

  Multiplexer_part #(.select(2)) multiplexer_1 (
    .in0(A0_2), .in1(A1_2), .in2(A2_2), .in3(A3_2), .out(multiplexer_1_out), .sel(S1_S0));  // open: en
  LED Output (.in(multiplexer_1_out));
  and and_1 (and_1_out, A0, ~S0, ~S1);  // AND_Gate
  and and_2 (and_2_out, A1, ~S0, S1);  // AND_Gate
  and and_3 (and_3_out, A2, S0, ~S1);  // AND_Gate
  and and_4 (and_4_out, A3, S0, S1);
  LED Output_2 (.in(or_1_out));
  or or_1 (or_1_out, and_1_out, and_2_out, and_3_out, and_4_out);
endmodule
