// Logisim project Storage.circ as structural Verilog: 3 circuits, main circuit SimpleFlipFlop
module SimpleFlipFlop (
  input  In
);

  wire or_1_out;

  or or_1 (or_1_out, In, or_1_out);
  LED Out (.in(or_1_out));

  // Notes on the sheet:
  //   Creative Commons BY NC 4.0 International License
endmodule

module SRFlipFlop (
  input  R,
  input  R_2,
  input  S,
  input  S_2
);

  wire nor_1_out, nor_2_out, or_1_out, or_2_out;

  nor nor_1 (nor_1_out, R, nor_2_out);
  nor nor_2 (nor_2_out, nor_1_out, S_2);
  // Probe on nor_1_out
  // Probe on nor_2_out
  // Probe on or_1_out
  or or_1 (or_1_out, R_2, or_2_out);
  or or_2 (or_2_out, or_1_out, S);
  // Probe on or_2_out

  // Notes on the sheet:
  //   Creative Commons BY NC 4.0 International License
  //   S-R Flip-Flop with OR Gates
  //   Both gates get stuck outputting a 1
endmodule

module WriteEnable (
  input  Set,
  input  R,
  input  Reset,
  input  EN,
  input  [1:0] Selector,
  input  S
);

  wire and_1_out, and_2_out, decoder_1_out0, decoder_1_out1, decoder_1_out2, decoder_1_out3, nor_1_out,
       nor_2_out;

  and and_1 (and_1_out, R, EN);
  and and_2 (and_2_out, EN, S);
  nor nor_1 (nor_1_out, and_1_out, nor_2_out);
  nor nor_2 (nor_2_out, nor_1_out, and_2_out);
  // Probe on nor_1_out
  // Probe on nor_2_out
  Decoder #(.select(2), .enable("false")) decoder_1 (
    .out0(decoder_1_out0), .out1(decoder_1_out1), .out2(decoder_1_out2), .out3(decoder_1_out3), .sel(Selector));
  S_R_Flip_Flop #(.trigger("high")) SR0__00 (
    .S(Set), .clk(decoder_1_out0), .R(Reset));  // open: Q, Qn, preset, reset, en
  S_R_Flip_Flop #(.trigger("high")) SR1__01 (
    .S(Set), .clk(decoder_1_out1), .R(Reset));  // open: Q, Qn, preset, reset, en
  S_R_Flip_Flop #(.trigger("high")) SR2__10 (
    .S(Set), .clk(decoder_1_out2), .R(Reset));  // open: Q, Qn, preset, reset, en
  S_R_Flip_Flop #(.trigger("high")) SR3__11 (
    .S(Set), .clk(decoder_1_out3), .R(Reset));  // open: Q, Qn, preset, reset, en

  // Notes on the sheet:
  //   Creative Commons BY NC 4.0 International License
endmodule
