// Logisim project Arithmetic.circ as structural Verilog: 6 circuits, main circuit HalfAdder
module HalfAdder (
  input  A,
  input  A_2,
  input  B,
  input  B_2
);

  wire _0_1_out, _1_0_out, _1_1_2_out, _1_1_out, or_1_out, xor_1_out;

  and _0_1 (_0_1_out, ~A, B);  // AND_Gate
  or or_1 (or_1_out, _0_1_out, _1_0_out);
  and _1_0 (_1_0_out, A, ~B);  // AND_Gate
  and _1_1 (_1_1_out, A, B);
  LED Sum (.in(or_1_out));
  LED Cout (.in(_1_1_out));
  LED Sum_2 (.in(xor_1_out));
  xor xor_1 (xor_1_out, A_2, B_2);
  LED Cout_2 (.in(_1_1_2_out));
  and _1_1_2 (_1_1_2_out, A_2, B_2);

  // Notes on the sheet:
  //   Creative Commons BY NC 4.0 International License
endmodule

module FullAdder (
  input  A,
  input  A_2,
  input  B,
  input  B_2,
  input  Cin,
  input  Cin_2,
  input  Cin_3,
  input  A_3,
  input  B_3
);

  wire _001_2_out, _001_out, _010_2_out, _010_out, _011_2_out, _011_out, _100_2_out, _100_out, _101_2_out,
       _101_out, _110_2_out, _110_out, _111_2_out, _111_3_out, _111_out, adder_1_cout, adder_1_out, or_1_out,
       or_2_out, or_3_out, or_4_out;

  and _001 (_001_out, ~A, ~B, Cin);  // AND_Gate
  and _010 (_010_out, ~A, B, ~Cin);  // AND_Gate
  and _100 (_100_out, A, ~B, ~Cin);  // AND_Gate
  and _111 (_111_out, A, B, Cin);
  and _011 (_011_out, ~A, B, Cin);  // AND_Gate
  and _101 (_101_out, A, ~B, Cin);  // AND_Gate
  and _110 (_110_out, A, B, ~Cin);  // AND_Gate
  and _111_2 (_111_2_out, A, B, Cin);
  or or_1 (or_1_out, _001_out, _010_out, _100_out, _111_out);
  LED Sum (.in(or_1_out));
  or or_2 (or_2_out, _011_out, _101_out, _110_out, _111_2_out);
  LED Cout (.in(or_2_out));
  LED Sum_2 (.in(adder_1_out));
  Adder #(.width(1)) adder_1 (.a(A_3), .b(B_3), .out(adder_1_out), .cin(Cin_3), .cout(adder_1_cout));
  LED Cout_2 (.in(adder_1_cout));
  and _001_2 (_001_2_out, ~A_2, ~B_2, Cin_2);  // AND_Gate
  and _010_2 (_010_2_out, ~A_2, B_2, ~Cin_2);  // AND_Gate
  and _100_2 (_100_2_out, A_2, ~B_2, ~Cin_2);  // AND_Gate
  and _011_2 (_011_2_out, ~A_2, B_2, Cin_2);  // AND_Gate
  and _101_2 (_101_2_out, A_2, ~B_2, Cin_2);  // AND_Gate
  and _110_2 (_110_2_out, A_2, B_2, ~Cin_2);  // AND_Gate
  and _111_3 (_111_3_out, A_2, B_2, Cin_2);
  or or_3 (or_3_out, _001_2_out, _010_2_out, _100_2_out, _111_3_out);
  LED Sum_3 (.in(or_3_out));
  or or_4 (or_4_out, _011_2_out, _101_2_out, _110_2_out, _111_3_out);
  LED Cout_3 (.in(or_4_out));

  // Notes on the sheet:
  //   Creative Commons BY NC 4.0 International License
endmodule

module RipplerAdder (
  input  A0,
  input  A1,
  input  A2,
  input  [3:0] A,
  input  A3,
  input  [3:0] B,
  input  B0,
  input  B1,
  input  B2,
  input  B3,
  output Sum0,
  output Sum1,
  output Sum2,
  output [3:0] Sum,
  output Sum3,
  output Overflow,
  output Overflow_2
);

  wire adder_1_cout, adder_2_cout, adder_3_cout;

  Adder #(.width(1)) adder_1 (.a(A0), .b(B0), .out(Sum0), .cin(1'b0), .cout(adder_1_cout));
  Adder #(.width(1)) adder_2 (.a(A1), .b(B1), .out(Sum1), .cin(adder_1_cout), .cout(adder_2_cout));
  Adder #(.width(1)) adder_3 (.a(A2), .b(B2), .out(Sum2), .cin(adder_2_cout), .cout(adder_3_cout));
  Adder #(.width(1)) adder_4 (.a(A3), .b(B3), .out(Sum3), .cin(adder_3_cout), .cout(Overflow_2));
  Adder #(.width(4)) adder_5 (.a(A), .b(B), .out(Sum), .cin(1'b0), .cout(Overflow));

  // Notes on the sheet:
  //   Creative Commons BY NC 4.0 International License
endmodule

module HalfSubtractor (
  input  A,
  input  A_2,
  input  A_3,
  input  B,
  input  B_2,
  input  B_3
);

  wire _0_1_2_out, _0_1_3_out, _0_1_4_out, _0_1_out, _1_0_2_out, _1_0_out, or_1_out, or_2_out, xor_1_out;

  and _0_1 (_0_1_out, ~A, B);  // AND_Gate
  and _1_0 (_1_0_out, A, ~B);  // AND_Gate
  and _0_1_2 (_0_1_2_out, ~A, B);  // AND_Gate
  or or_1 (or_1_out, _0_1_out, _1_0_out);
  LED D (.in(or_1_out));
  LED Bout (.in(_0_1_2_out));
  and _0_1_3 (_0_1_3_out, ~A_2, B_2);  // AND_Gate
  and _1_0_2 (_1_0_2_out, A_2, ~B_2);  // AND_Gate
  or or_2 (or_2_out, _0_1_3_out, _1_0_2_out);
  LED D_2 (.in(or_2_out));
  LED Bout_2 (.in(_0_1_3_out));
  xor xor_1 (xor_1_out, A_3, B_3);
  LED D_3 (.in(xor_1_out));
  and _0_1_4 (_0_1_4_out, ~A_3, B_3);  // AND_Gate
  LED Bout_3 (.in(_0_1_4_out));

  // Notes on the sheet:
  //   Creative Commons BY NC 4.0 International License
endmodule

module FullSubtractor (
  input  A,
  input  B,
  input  Bin,
  input  Bin_2,
  input  A_2,
  input  B_2
);

  wire _001_out, _010_out, _011_out, _100_out, _111_out, or_1_out, or_2_out, subtractor_1_bout,
       subtractor_1_out;

  and _001 (_001_out, ~A, ~B, Bin);  // AND_Gate
  and _010 (_010_out, ~A, B, ~Bin);  // AND_Gate
  and _100 (_100_out, A, ~B, ~Bin);  // AND_Gate
  and _111 (_111_out, A, B, Bin);
  and _011 (_011_out, ~A, B, Bin);  // AND_Gate
  LED D (.in(or_1_out));
  or or_1 (or_1_out, _001_out, _010_out, _100_out, _111_out);
  or or_2 (or_2_out, _001_out, _010_out, _111_out, _011_out);
  LED Bout (.in(or_2_out));
  LED D_2 (.in(subtractor_1_out));
  Subtractor #(.width(1)) subtractor_1 (
    .a(A_2), .b(B_2), .out(subtractor_1_out), .bin(Bin_2), .bout(subtractor_1_bout));
  LED Bout_2 (.in(subtractor_1_bout));

  // Notes on the sheet:
  //   Creative Commons BY NC 4.0 International License
endmodule

module RippleSubtractor (
  input  A0,
  input  A1,
  input  A2,
  input  [3:0] A,
  input  A3,
  input  [3:0] B,
  input  B0,
  input  B1,
  input  B2,
  input  B3,
  output Diff0,
  output Diff1,
  output Diff2,
  output [3:0] Sum,
  output Diff3,
  output Overflow,
  output Underflow
);

  wire subtractor_1_bout, subtractor_2_bout, subtractor_3_bout;

  Subtractor #(.width(1)) subtractor_1 (.a(A0), .b(B0), .out(Diff0), .bin(1'b0), .bout(subtractor_1_bout));
  Subtractor #(.width(1)) subtractor_2 (.a(A1), .b(B1), .out(Diff1), .bin(subtractor_1_bout), .bout(subtractor_2_bout));
  Subtractor #(.width(1)) subtractor_3 (.a(A2), .b(B2), .out(Diff2), .bin(subtractor_2_bout), .bout(subtractor_3_bout));
  Subtractor #(.width(1)) subtractor_4 (.a(A3), .b(B3), .out(Diff3), .bin(subtractor_3_bout), .bout(Underflow));
  Subtractor #(.width(4)) subtractor_5 (.a(A), .b(B), .out(Sum), .bin(1'b0), .bout(Overflow));

  // Notes on the sheet:
  //   Creative Commons BY NC 4.0 International License
endmodule
