// Logisim project Control.circ as structural Verilog: 2 circuits, main circuit Decoder
module Decoder (
  input  A,
  input  B,
  input  Bit8,
  input  Bit7,
  input  [1:0] A_B
);

  wire Add_out, and_1_out, and_2_out, and_3_out, and_4_out, decoder_1_out0, decoder_1_out1, decoder_1_out2,
       decoder_1_out3, Div_out, Mul_out, Sub_out;

  Decoder_part #(.select(2)) decoder_1 (
    .out0(decoder_1_out0), .out1(decoder_1_out1), .out2(decoder_1_out2), .out3(decoder_1_out3), .sel(A_B));  // open: en
  LED D0 (.in(and_1_out));
  and and_1 (and_1_out, ~A, ~B);  // AND_Gate
  and and_2 (and_2_out, ~A, B);  // AND_Gate
  LED D1 (.in(and_2_out));
  LED D2 (.in(and_3_out));
  and and_3 (and_3_out, A, ~B);  // AND_Gate
  and and_4 (and_4_out, A, B);
  LED D3 (.in(and_4_out));
  LED D0_2 (.in(decoder_1_out0));
  LED D1_2 (.in(decoder_1_out1));
  LED D2_2 (.in(decoder_1_out2));
  LED D3_2 (.in(decoder_1_out3));
  and Add (Add_out, ~Bit8, ~Bit7);  // AND_Gate
  and Sub (Sub_out, ~Bit8, Bit7);  // AND_Gate
  and Mul (Mul_out, Bit8, ~Bit7);  // AND_Gate
  and Div (Div_out, Bit8, Bit7);

  // Notes on the sheet:
  //   Creative Commons BY NC 4.0 International License
  //   Input to
  //   Operation
  //   Selector
endmodule

module Multiplexer (
  input  A3,
  input  A2,
  input  A1,
  input  A0,
  input  KB,
  input  RAM,
  input  Temp,
  input  L1,
  input  S0,
  input  Bit_2,
  input  S1,
  input  Bit_1,
  input  A3_2,
  input  A2_2,
  input  A1_2,
  input  A0_2,
  input  S0_2,
  input  S1_2,
  input  A3_3,
  input  A2_3,
  input  A1_3,
  input  A0_3,
  input  [1:0] S1_S0,
  input  Enable
);

  wire _0_0_2_out, _0_0_out, _0_1_2_out, _0_1_out, _1_0_2_out, _1_0_out, _1_1_2_out, _1_1_out, and_1_out,
       and_2_out, and_3_out, and_4_out, multiplexer_1_out, not_1_out, not_2_out, not_3_out, not_4_out,
       not_5_out, not_6_out, not_7_out, not_8_out, or_1_out, or_2_out, or_3_out;

  not not_1 (not_1_out, S0);
  and _0_0 (_0_0_out, A0, not_1_out, not_2_out);
  not not_2 (not_2_out, S1);
  and _0_1 (_0_1_out, A1, not_3_out, S1);
  not not_3 (not_3_out, S0);
  and _1_0 (_1_0_out, A2, S0, not_4_out);
  not not_4 (not_4_out, S1);
  and _1_1 (_1_1_out, A3, S0, S1);
  not not_5 (not_5_out, S0_2);
  not not_6 (not_6_out, S1_2);
  not not_7 (not_7_out, S0_2);
  not not_8 (not_8_out, S1_2);
  and _0_0_2 (_0_0_2_out, A0_2, not_5_out, not_6_out, Enable);
  and _0_1_2 (_0_1_2_out, A1_2, not_7_out, S1_2, Enable);
  and _1_0_2 (_1_0_2_out, A2_2, S0_2, not_8_out, Enable);
  and _1_1_2 (_1_1_2_out, A3_2, S0_2, S1_2, Enable);
  LED Output (.in(or_1_out));
  or or_1 (or_1_out, _0_0_out, _0_1_out, _1_0_out, _1_1_out);
  LED Output_2 (.in(or_2_out));
  or or_2 (or_2_out, _0_0_2_out, _0_1_2_out, _1_0_2_out, _1_1_2_out);
  and and_1 (and_1_out, L1, ~Bit_2, ~Bit_1);  // AND_Gate
  and and_2 (and_2_out, Temp, ~Bit_2, Bit_1);  // AND_Gate
  and and_3 (and_3_out, RAM, Bit_2, ~Bit_1);  // AND_Gate
  and and_4 (and_4_out, KB, Bit_2, Bit_1);
  or or_3 (or_3_out, and_1_out, and_2_out, and_3_out, and_4_out);
  LED led_1 (.in(or_3_out));
  Multiplexer_part #(.select(2)) multiplexer_1 (
    .in0(A0_3), .in1(A1_3), .in2(A2_3), .in3(A3_3), .out(multiplexer_1_out), .sel(S1_S0));  // open: en
  LED Output_3 (.in(multiplexer_1_out));

  // Notes on the sheet:
  //   Creative Commons BY NC 4.0 International License
  //   Output to
  //   next circuit
endmodule
