// Logisim project Design.circ as structural Verilog: 1 circuit, main circuit Ambiguities
module Ambiguities (
  input  A,
  input  A_2,
  input  B,
  input  B_2,
  input  C,
  input  C_2
);

  wire _0_0_1_out, _0_1_1_out, _0_1_2_out, _0_1_out, _1_0_0_out, _1_0_out, _1_1_0_out, _1__0_out, or_1_out,
       or_2_out;

  and _0_0_1 (_0_0_1_out, ~A, ~B, C);  // AND_Gate
  and _0_1_1 (_0_1_1_out, ~A, B, C);  // AND_Gate
  and _1_0_0 (_1_0_0_out, A, ~B, ~C);  // AND_Gate
  and _1_1_0 (_1_1_0_out, A, B, ~C);  // AND_Gate
  or or_1 (or_1_out, _0_0_1_out, _0_1_1_out, _1_0_0_out, _1_1_0_out);
  LED Zout (.in(or_1_out));
  and _0_1 (_0_1_out, ~A_2, C_2);  // AND_Gate
  and _0_1_2 (_0_1_2_out, ~A_2, C_2);  // AND_Gate
  and _1__0 (_1__0_out, A_2, ~C_2);  // AND_Gate
  and _1_0 (_1_0_out, A_2, ~C_2);  // AND_Gate
  or or_2 (or_2_out, _0_1_out, _0_1_2_out, _1__0_out, _1_0_out);
  LED Zout_2 (.in(or_2_out));

  // Notes on the sheet:
  //   Circuit from 3-Step Algorithm
  //   CSC 131 - Allan Hancock College - Mark Kozel (MKozel@HancockCollege.edu) - Attribution-NonCommercial-ShareAlike 4.0 International (CC BY-NC-SA 4.0)
  //   Remove the B input and simplify the gates
endmodule
