// Logisim project TTAlgorithm.circ as structural Verilog: 3 circuits, main circuit SimpleExample
module SimpleExample (
  input  A,
  input  A_2,
  input  A_3,
  input  B,
  input  B_2,
  input  B_3,
  input  C,
  input  C_2,
  input  C_3
);

  wire _0_0_1_3_out, _1_1_0_3_out, not_1_out, not_2_out, or_1_out;

  // AND_Gate _0_0_1 is placed but not wired
  // AND_Gate _1_1_0 is placed but not wired
  not not_1 (not_1_out, C_2);
  // AND_Gate _0_0_1_2 has open pins: in0=A_2, in1=B_2, in2=C_2, out=open
  // AND_Gate _1_1_0_2 has open pins: in0=A_2, in1=B_2, in2=not_1_out, out=open
  and _0_0_1_3 (_0_0_1_3_out, ~A_3, ~B_3, C_3);  // AND_Gate
  and _1_1_0_3 (_1_1_0_3_out, A_3, B_3, not_2_out);
  not not_2 (not_2_out, C_3);
  or or_1 (or_1_out, _0_0_1_3_out, _1_1_0_3_out);
  LED Zout (.in(or_1_out));

  // Notes on the sheet:
  //   1. Add an AND gate for each 1 output
  //   Creative Commons BY NC 4.0 International License
  //   2. Negate each AND gate input
  //   where the value is zero (0)
  //   3. Connect Outputs of each
  //   AND gate to an OR gate
endmodule

module MultiOutputs (
  input  A,
  input  A_2,
  input  A_3,
  input  B,
  input  B_2,
  input  B_3,
  input  C,
  input  C_2,
  input  C_3
);

  wire _0_0_0_3_out, _0_0_1_3_out, _1_1_0_5_out, _1_1_0_6_out, or_1_out, or_2_out;

  // AND_Gate _0_0_0 is placed but not wired
  // AND_Gate _1_1_0 is placed but not wired
  // AND_Gate _0_0_1 is placed but not wired
  // AND_Gate _1_1_0_2 is placed but not wired
  // AND_Gate _0_0_0_2 has open pins: in0=A_2, in1=B_2, in2=C_2, out=open
  // AND_Gate _1_1_0_3 has open pins: in0=A_2, in1=B_2, in2=C_2, out=open
  // AND_Gate _0_0_1_2 has open pins: in0=A_2, in1=B_2, in2=C_2, out=open
  // AND_Gate _1_1_0_4 has open pins: in0=A_2, in1=B_2, in2=C_2, out=open
  and _0_0_0_3 (_0_0_0_3_out, ~A_3, ~B_3, ~C_3);  // AND_Gate
  and _1_1_0_5 (_1_1_0_5_out, A_3, B_3, ~C_3);  // AND_Gate
  and _0_0_1_3 (_0_0_1_3_out, ~A_3, ~B_3, C_3);  // AND_Gate
  and _1_1_0_6 (_1_1_0_6_out, A_3, B_3, ~C_3);  // AND_Gate
  LED Yout (.in(or_1_out));
  or or_1 (or_1_out, _0_0_0_3_out, _1_1_0_5_out);
  LED Zout (.in(or_2_out));
  or or_2 (or_2_out, _0_0_1_3_out, _1_1_0_6_out);

  // Notes on the sheet:
  //   1. Add an AND gate for each 1 output
  //   Creative Commons BY NC 4.0 International License
  //   2. Negate each AND gate input
  //   where the value is zero (0)
  //   3. Connect Outputs of each
  //   AND gate to an OR gate
endmodule

module Optimize (
  input  A,
  input  A_2,
  input  B,
  input  B_2,
  input  C,
  input  C_2
);

  wire _0_0_0_2_out, _0_0_0_out, _0_0_1_2_out, _0_0_1_out, _1_1_0_2_out, _1_1_0_3_out, _1_1_0_out, or_1_out,
       or_2_out, or_3_out, or_4_out;

  and _0_0_0 (_0_0_0_out, ~A, ~B, ~C);  // AND_Gate
  and _1_1_0 (_1_1_0_out, A, B, ~C);  // AND_Gate
  and _0_0_1 (_0_0_1_out, ~A, ~B, C);  // AND_Gate
  and _1_1_0_2 (_1_1_0_2_out, A, B, ~C);  // AND_Gate
  or or_1 (or_1_out, _0_0_0_out, _1_1_0_out);
  LED Yout (.in(or_1_out));
  or or_2 (or_2_out, _0_0_1_out, _1_1_0_2_out);
  LED Zout (.in(or_2_out));
  and _0_0_0_2 (_0_0_0_2_out, ~A_2, ~B_2, ~C_2);  // AND_Gate
  and _1_1_0_3 (_1_1_0_3_out, A_2, B_2, ~C_2);  // AND_Gate
  and _0_0_1_2 (_0_0_1_2_out, ~A_2, ~B_2, C_2);  // AND_Gate
  LED Yout_2 (.in(or_3_out));
  or or_3 (or_3_out, _0_0_0_2_out, _1_1_0_3_out);
  LED Zout_2 (.in(or_4_out));
  or or_4 (or_4_out, _1_1_0_3_out, _0_0_1_2_out);

  // Notes on the sheet:
  //   Creative Commons BY NC 4.0 International License
endmodule
