// Logisim project Transistors.circ as structural Verilog: 1 circuit, main circuit Transistors
module Transistors (
  input  Control
);

  wire transistor_1_out, transistor_2_out;

  Transistor transistor_1 (.in(1'b1), .out(transistor_1_out), .gate(Control));
  Transistor #(.\type ("n")) transistor_2 (.in(1'b1), .out(transistor_2_out), .gate(Control));
  // Probe on transistor_1_out
  // Probe on transistor_2_out

  // Notes on the sheet:
  //   Source
  //   Drain
  //   Source
  //   Drain
  //   P-Type
  //   N-Type
  //   Creative Commons BY NC 4.0 International License
endmodule
